// Logisim project cpu.circ as structural Verilog: 11 circuits, main circuit main
module main (
  input  reset
);

  wire clk, cpu_1_out_8;
  wire [5:0] cpu_1_out_7;
  wire [7:0] cpu_1_out_5, cpu_1_out_6, ram_1_data, rom_1_data;

  Clock u_clk (.out(clk));
  CPU cpu_1 (
    .in_1(clk), .in_2(rom_1_data), .in_3(reset), .in_4(ram_1_data), .out_5(cpu_1_out_5), .out_6(cpu_1_out_6),
    .out_7(cpu_1_out_7), .out_8(cpu_1_out_8));
  RAM #(.bus("separate")) ram_1 (
    .addr(cpu_1_out_6), .din(cpu_1_out_5), .data(ram_1_data), .str(cpu_1_out_8), .clk(clk), .ld(1'b1),
    .clr(reset));  // open: sel
  ROM #(.addrWidth(6)) rom_1 (.addr(cpu_1_out_7), .data(rom_1_data));  // open: sel
endmodule

module meiasoma (
  input  input_a,
  input  input_b,
  output \output ,
  output carry
);

  wire or_1_out;

  or or_1 (or_1_out, input_b, input_a);
  and and_1 (carry, input_a, input_b);
  and and_2 (\output , or_1_out, ~carry);  // AND_Gate
endmodule

module somacompleta (
  input  input_x,
  input  input_y,
  input  input_z,
  output \output ,
  output carry
);

  wire and_1_out, and_2_out, and_3_out, and_4_out, or_1_out, or_2_out;

  or or_1 (or_1_out, input_z, input_y);
  and and_1 (and_1_out, input_y, input_z);
  and and_2 (and_2_out, or_1_out, ~and_1_out);  // AND_Gate
  and and_3 (and_3_out, input_x, and_2_out);
  or or_2 (or_2_out, input_x, and_2_out);
  and and_4 (and_4_out, input_x, and_2_out);
  or or_3 (carry, and_3_out, and_1_out);
  and and_5 (\output , or_2_out, ~and_4_out);  // AND_Gate
endmodule

module somacompleta2 (
  input  in_1,
  input  in_2,
  input  in_3,
  output out_4,
  output out_5
);

  wire meiasoma_1_carry, meiasoma_1_output, meiasoma_2_carry;

  meiasoma meiasoma_1 (.input_a(in_2), .input_b(in_3), .\output (meiasoma_1_output), .carry(meiasoma_1_carry));
  meiasoma meiasoma_2 (.input_a(in_1), .input_b(meiasoma_1_output), .\output (out_4), .carry(meiasoma_2_carry));
  or or_1 (out_5, meiasoma_2_carry, meiasoma_1_carry);
endmodule

module soma (
  input  [3:0] in_1,
  input  [3:0] in_2,
  output [3:0] out_3
);

  wire somacompleta2_1_out_5, somacompleta2_2_out_5, somacompleta2_3_out_5, somacompleta2_4_out_5;

  // Probe on in_1
  // Probe on in_2
  somacompleta2 somacompleta2_1 (
    .in_1(in_1[0]), .in_2(in_2[0]), .in_3(1'b0), .out_4(out_3[0]), .out_5(somacompleta2_1_out_5));
  somacompleta2 somacompleta2_2 (
    .in_1(somacompleta2_1_out_5), .in_2(in_1[1]), .in_3(in_2[1]), .out_4(out_3[1]),
    .out_5(somacompleta2_2_out_5));
  somacompleta2 somacompleta2_3 (
    .in_1(somacompleta2_2_out_5), .in_2(in_1[2]), .in_3(in_2[2]), .out_4(out_3[2]),
    .out_5(somacompleta2_3_out_5));
  somacompleta2 somacompleta2_4 (
    .in_1(somacompleta2_3_out_5), .in_2(in_1[3]), .in_3(in_2[3]), .out_4(out_3[3]),
    .out_5(somacompleta2_4_out_5));
  // Probe on out_3
  // Probe on somacompleta2_4_out_5

  // Other names for the same wires on the sheet: a1 = in_1[0]; a2 = in_1[1]; a3 = in_1[2]; a4 = in_1[3]; b1 = in_2[0];
  //   b2 = in_2[1]; b3 = in_2[2]; b4 = in_2[3]
endmodule

module ULA (
  input  [7:0] A,
  input  [1:0] OP,
  input  [7:0] B,
  output [7:0] out_4,
  output out_5,
  output out_6
);

  wire [7:0] \and , multi, \or , sum;

  // Probe on A
  // Probe on B
  Adder adder_1 (.a(A), .b(B), .out(sum));  // open: cin, cout
  Multiplier multiplier_1 (.a(A), .b(B), .out(multi));  // open: cin, cout
  assign \or  = A | B;  // OR_Gate or_1, 8 bits wide
  assign \and  = A & B;  // AND_Gate and_1, 8 bits wide
  Comparator #(.mode("unsigned")) comparator_1 (.a(A), .b(B), .gt(out_5), .lt(out_6));  // open: eq
  // Probe on out_4
  Multiplexer #(.select(2), .width(8)) multiplexer_1 (
    .in0(sum), .in1(multi), .in2(\or ), .in3(\and ), .out(out_4), .sel(OP));  // open: en
endmodule

module Latch (
  input  S,
  input  R,
  output Q
);

  wire and_1_out, and_2_out, not_1_out, not_2_out, not_4_out;

  not not_1 (not_1_out, S);
  not not_2 (not_2_out, R);
  not not_3 (Q, and_1_out);
  and and_1 (and_1_out, not_1_out, not_4_out);
  not not_4 (not_4_out, and_2_out);
  and and_2 (and_2_out, Q, not_2_out);
endmodule

module FlipFlop (
  input  a,
  input  clk,
  input  enable,
  input  reset,
  output out_5
);

  wire and_1_out, and_2_out, and_3_out, not_1_out, or_1_out;

  not not_1 (not_1_out, a);
  and and_1 (and_1_out, clk, enable);
  and and_2 (and_2_out, a, and_1_out);
  and and_3 (and_3_out, and_1_out, not_1_out);
  or or_1 (or_1_out, and_3_out, reset);
  Latch latch_1 (.S(and_2_out), .R(or_1_out), .Q(out_5));
endmodule

module Register (
  input  clk,
  input  \input ,
  input  enable,
  input  reset,
  output out_5
);

  wire flipflop_1_out_5, not_1_out;

  FlipFlop flipflop_1 (.a(\input ), .clk(clk), .enable(enable), .reset(reset), .out_5(flipflop_1_out_5));
  not not_1 (not_1_out, clk);
  FlipFlop flipflop_2 (.a(flipflop_1_out_5), .clk(not_1_out), .enable(enable), .reset(reset), .out_5(out_5));
endmodule

module REGS (
  input  [1:0] adda,
  input  [1:0] addb,
  input  [7:0] \input ,
  input  clk,
  input  reset,
  input  enable,
  output [7:0] out_7,
  output [7:0] out_8
);

  wire en0, en1, en2, en3;
  wire [7:0] _0, _1, _2, _3;

  Demultiplexer #(.select(2)) demultiplexer_1 (
    .out0(en0), .out1(en1), .out2(en2), .out3(en3), .in(enable), .sel(adda));  // open: en
  Register_part register_1 (.D(\input ), .en(en0), .Q(_0), .clk(clk), .clr(reset));
  Register_part register_2 (.D(\input ), .en(en2), .Q(_2), .clk(clk), .clr(reset));
  Register_part register_3 (.D(\input ), .en(en1), .Q(_1), .clk(clk), .clr(reset));
  Register_part register_4 (.D(\input ), .en(en3), .Q(_3), .clk(clk), .clr(reset));
  Multiplexer #(.select(2), .width(8)) multiplexer_1 (
    .in0(_0), .in1(_1), .in2(_2), .in3(_3), .out(out_7), .sel(adda));  // open: en
  Multiplexer #(.select(2), .width(8)) multiplexer_2 (
    .in0(_0), .in1(_1), .in2(_2), .in3(_3), .out(out_8), .sel(addb));  // open: en

  // Other names for the same wires on the sheet: a[1:0] = adda; b[1:0] = addb; en = enable
endmodule

module CPU (
  input  in_1,
  input  [7:0] in_2,
  input  in_3,
  input  [7:0] in_4,
  output [7:0] out_5,
  output [7:0] out_6,
  output [5:0] out_7,
  output out_8
);

  wire movecons, regen;
  wire [1:0] aab, adda, op;
  wire [5:0] nextline;
  wire [7:0] constant, multiplexer_1_out, outula, regs_1_out_7, regs_1_out_8;

  Multiplexer #(.width(8)) multiplexer_1 (
    .in0(outula), .in1(constant), .out(multiplexer_1_out), .sel(movecons));  // open: en
  REGS regs_1 (
    .adda(adda), .addb(aab), .\input (multiplexer_1_out), .clk(in_1), .reset(in_3), .enable(regen),
    .out_7(regs_1_out_7), .out_8(regs_1_out_8));
  Register_part #(.width(6)) register_1 (.D(nextline), .en(in_1), .Q(out_7), .clk(in_1), .clr(in_3));
  // Probe on regs_1_out_7
  // Probe on regs_1_out_8
  ULA ula_1 (.A(regs_1_out_7), .OP(op), .B(regs_1_out_8), .out_4(outula));  // open: out_5, out_6
  // Probe on outula
  // Probe on nextline
  Adder #(.width(6)) adder_1 (.a(out_7), .b(6'b000001), .out(nextline));  // open: cin, cout

  // Other names for the same wires on the sheet: clk = in_1; memoryin[7:0] = out_5; memoryout[7:0] = in_4;
  //   memoyadd[7:0] = out_6; opcode[7:0] = in_2; PC[5:0] = out_7; reset = in_3; str = out_8
endmodule
